# Fritzing sketch Schema_dev (saved by Fritzing 0.9.3b)
breadboards: 1

parts:
  Bauteil1 = Arduino Uno (Rev3)
  LED1 = LED - 3mm [color="Red (633nm)" package="3 mm [THT]"]
  LED2 = LED - 3mm [color="Red (633nm)" package="3 mm [THT]"]
  S1 = Momentary Switch [package=ksa_sealed_tac_switch]
  S2 = Momentary Switch [package=ksa_sealed_tac_switch]
  R1 = Resistor [tolerance=±5% resistance=220 package=THT]
  R2 = Resistor [tolerance=±5% resistance=220 package="2512 [SMD]"]
  R3 = Resistor [tolerance=±5% resistance=220 package="2512 [SMD]"]
  R4 = Resistor [tolerance=±5% resistance=220 package="0402 [SMD]"]

nets:
  N1: Bauteil1.D12/MISO, LED2.cathode
  N2: Bauteil1.D13/SCK, LED1.cathode
  N3: Bauteil1.D6_PWM, S2.1
  N4: Bauteil1.D7, S1.1
  N5: LED1.anode, R3.Pin_0
  N6: LED2.anode, R2.Pin_0
  N7: S1.2, R4.Pin_0
  N8: S1.4, S2.4
  N9: S2.2, R1.Pin_0
  N10: R1.Pin_1, R2.Pin_1, R3.Pin_1, R4.Pin_1
