# Fritzing sketch Schematic (saved by Fritzing 0.9.3b)
circuit board: 6.88566cm x 5.36311cm
breadboards: 1

parts:
  1 = Pushbutton [package=THT]
  2 = Pushbutton [package=THT]
  3 = Pushbutton [package=THT]
  4 = Pushbutton [package=THT]
  UNO = Arduino Uno (Rev3)
  LED1 = LED - 5mm [color="Red (633nm)" package="5 mm [THT]"]
  LED2 = LED - 5mm [color="Red (633nm)" package="5 mm [THT]"]
  LED3 = LED - 5mm [color="Red (633nm)" package="5 mm [THT]"]
  LED4 = LED - 5mm [color="Red (633nm)" package="5 mm [THT]"]
  R1 = Resistor [tolerance=±5% resistance=220 package=THT]
  R2 = Resistor [tolerance=±5% resistance=220 package=THT]
  R3 = Resistor [tolerance=±5% resistance=220 package=THT]
  R4 = Resistor [tolerance=±5% resistance=220 package=THT]

nets:
  N1: 1.leg0, UNO.D4
  N2: 1.leg1, 2.leg1, 3.leg1, 4.leg1, UNO.D2
  N3: 2.leg0, UNO.D5_PWM
  N4: 3.leg0, UNO.D6_PWM
  N5: 4.leg0, UNO.D7
  N6: UNO.D10_PWM/SS, LED1.anode
  N7: UNO.D11_PWM/MOSI, LED2.anode
  N8: UNO.D12/MISO, LED3.anode
  N9: UNO.D13/SCK, LED4.anode
  N10: UNO.GND, R1.Pin_1, R2.Pin_1, R3.Pin_1, R4.Pin_1
  N11: LED1.cathode, R1.Pin_0
  N12: LED2.cathode, R2.Pin_0
  N13: LED3.cathode, R3.Pin_0
  N14: LED4.cathode, R4.Pin_0

notes:
  Svizel_pritula
